// Digital circuit Register-File.dig as structural Verilog
module Register_File (
  input  [1:0] Select_Read1,
  input  [1:0] Select_Read2,
  input  [3:0] Write_Data,
  input  [1:0] Select_Write,
  input  [7:0] Ctrl_Registers,
  input  clk,
  output [3:0] Read_Data_1,
  output [3:0] Read_Data_2
);

  wire [3:0] demultiplexer_1_out_0, demultiplexer_1_out_1, demultiplexer_1_out_2, demultiplexer_1_out_3,
       R_0_p4, R_1_p4, R_2_p4, R_3_p4;

  Demultiplexer #(.Selector_Bits(2), .Bits(4)) demultiplexer_1 (
    .sel(Select_Write), .in(Write_Data), .out_0(demultiplexer_1_out_0), .out_1(demultiplexer_1_out_1),
    .out_2(demultiplexer_1_out_2), .out_3(demultiplexer_1_out_3));
  // _4_bit_IR R_0: pin names not known; wires that end beside it: clk, Ctrl_Registers[1:0], demultiplexer_1_out_0, R_0_p4
  // _4_bit_IR R_1: pin names not known; wires that end beside it: clk, Ctrl_Registers[3:2], demultiplexer_1_out_1, R_1_p4
  // _4_bit_IR R_2: pin names not known; wires that end beside it: clk, Ctrl_Registers[5:4], demultiplexer_1_out_2, R_2_p4
  // _4_bit_IR R_3: pin names not known; wires that end beside it: clk, Ctrl_Registers[7:6], demultiplexer_1_out_3, R_3_p4
  Multiplexer #(.Selector_Bits(2), .Bits(4)) multiplexer_1 (
    .sel(Select_Read1), .in_0(R_0_p4), .in_1(R_1_p4), .in_2(R_2_p4), .in_3(R_3_p4), .out(Read_Data_1));
  Multiplexer #(.Selector_Bits(2), .Bits(4)) multiplexer_2 (
    .sel(Select_Read2), .in_0(R_0_p4), .in_1(R_1_p4), .in_2(R_2_p4), .in_3(R_3_p4), .out(Read_Data_2));
endmodule
